// Digital circuit 8WayOr.dig as structural Verilog
module _8WayOr (
  input  A,
  input  B,
  input  C,
  input  D,
  input  E,
  input  F,
  input  G,
  input  H,
  output out_9
);

  wire or_1_out, or_2_out, or_3_out, or_4_out, or_5_out, or_6_out;

  or or_1 (or_1_out, A, B);
  or or_2 (or_2_out, C, D);
  or or_3 (or_3_out, E, F);
  or or_4 (or_4_out, G, H);
  or or_5 (or_5_out, or_1_out, or_2_out);
  or or_6 (or_6_out, or_3_out, or_4_out);
  or or_7 (out_9, or_5_out, or_6_out);
endmodule
