// Digital circuit Mux.dig as structural Verilog
module Mux (
  input  A,
  input  B,
  input  Sel,
  output out_4
);

  wire and_1_out, and_2_out, not_1_out;

  and and_1 (and_1_out, A, not_1_out);
  not not_1 (not_1_out, Sel);
  and and_2 (and_2_out, B, Sel);
  or or_1 (out_4, and_1_out, and_2_out);
endmodule
