// Digital circuit Or.dig as structural Verilog
module Or (
  input  in_2,
  input  in_3,
  output out_1
);

  wire nand_1_out, nand_2_out;

  nand nand_1 (nand_1_out, in_2, in_2);
  nand nand_2 (nand_2_out, in_3, in_3);
  nand nand_3 (out_1, nand_1_out, nand_2_out);
endmodule
