// Digital circuit Xor.dig as structural Verilog
module Xor (
  input  in_1,
  input  in_2,
  output out_3
);

  wire nand_1_out, or_1_out;

  nand nand_1 (nand_1_out, in_1, in_2);
  or or_1 (or_1_out, in_1, in_2);
  and and_1 (out_3, nand_1_out, or_1_out);
endmodule
