// Digital circuit ALU.dig as structural Verilog
module ALU (
  input  [15:0] x,
  input  [15:0] y,
  input  zx,
  input  nx,
  input  zy,
  input  ny,
  input  f,
  input  no,
  output Out,
  output zr,
  output ng
);

  wire [15:0] and_1_out, fulladder_1_p4, multiplexer_1_out, multiplexer_2_out, multiplexer_5_out, not_1_out,
       not_2_out, not_3_out, RdyX, RdyY;

  Multiplexer #(.Bits(16)) multiplexer_1 (.sel(zx), .in_0(x), .in_1({16{1'b0}}), .out(multiplexer_1_out));
  Multiplexer #(.Bits(16)) multiplexer_2 (.sel(zy), .in_0(y), .in_1({16{1'b0}}), .out(multiplexer_2_out));
  assign not_1_out = ~multiplexer_1_out;  // Not not_1, 16 bits wide
  assign not_2_out = ~multiplexer_2_out;  // Not not_2, 16 bits wide
  Multiplexer multiplexer_3 (.sel(nx), .in_0(multiplexer_1_out[0]), .in_1(not_1_out[0]), .out(RdyX[0]));
  Multiplexer multiplexer_4 (.sel(ny), .in_0(multiplexer_2_out[0]), .in_1(not_2_out[0]), .out(RdyY[0]));
  assign and_1_out = RdyX & RdyY;  // And and_1, 16 bits wide
  // FullAdder fulladder_1: pin names not known; wires that end beside it: RdyX, RdyY, 1'b0, fulladder_1_p4, zr
  Multiplexer #(.Bits(16)) multiplexer_5 (.sel(f), .in_0(and_1_out), .in_1(fulladder_1_p4), .out(multiplexer_5_out));
  assign not_3_out = ~multiplexer_5_out;  // Not not_3, 16 bits wide
  Multiplexer multiplexer_6 (.sel(no), .in_0(multiplexer_5_out[0]), .in_1(not_3_out[0]), .out(Out));
  // Pins of 1 and 16 bits meet at multiplexer_1_out
  // Pins of 1 and 16 bits meet at multiplexer_2_out
  // Pins of 1 and 16 bits meet at RdyX
  // Pins of 1 and 16 bits meet at RdyY
  // Pins of 1 and 16 bits meet at multiplexer_5_out
  // Pins of 1 and 16 bits meet at not_3_out
  // Pins of 1 and 16 bits meet at not_1_out
  // Pins of 1 and 16 bits meet at not_2_out

  // Other names for the same wires on the sheet: RdyOut[15] = ng
endmodule
